// Logisim project CPU.circ as structural Verilog: 6 circuits, main circuit main
module main (
);

  wire ALU_carry_out, alusrc, Ci, clock, dispwe, halt, memwe, regwe;
  wire [1:0] pcsrc, regsrc;
  wire [2:0] btype, rdidx, rsidx;
  wire [3:0] aluop, display_1_hi_2, display_1_lo_2, display_1_lo_3, display_1_lo_4;
  wire [7:0] alu, data, imm, multiplexer_1_out, multiplexer_2_out, PC, PC_1, rd, rs;
  wire [15:0] rom_1_data;

  PC u_PC (.REG_rd(rd), .imm(imm), .PC(PC), .PCSrc(pcsrc), .HALT(halt), .Clock(clock), .PC_1(PC_1), .btype(btype));
  LED u_HALT (.in(halt));
  Display display_1 (
    .hi(rs), .lo(rd), .Enable(dispwe), .Clock(clock), .hi_2(display_1_hi_2), .lo_2(display_1_lo_2),
    .lo_3(display_1_lo_3), .lo_4(display_1_lo_4));
  ROM #(.dataWidth(16)) rom_1 (.addr(PC), .data(rom_1_data));  // open: sel
  Control control_1 (
    .ROM_instruction(rom_1_data), .rdidx(rdidx), .rsidx(rsidx), .imm(imm), .halt(halt), .dispwe(dispwe),
    .memwe(memwe), .aluop(aluop), .alusrc(alusrc), .regwe(regwe), .regsrc(regsrc), .pcsrc(pcsrc),
    .btype(btype));
  Clock clock_1 (.out(clock));
  Hex_Digit_Display hex_digit_display_1 (.value(display_1_hi_2));  // open: dp
  Hex_Digit_Display hex_digit_display_2 (.value(display_1_lo_2));  // open: dp
  Multiplexer #(.select(2), .width(8)) multiplexer_1 (
    .in0(alu), .in1(data), .in2(imm), .in3(PC_1), .out(multiplexer_1_out), .sel(regsrc));  // open: en
  Hex_Digit_Display hex_digit_display_3 (.value(display_1_lo_4));  // open: dp
  Hex_Digit_Display hex_digit_display_4 (.value(display_1_lo_3));  // open: dp
  Register_File REG (
    .data(multiplexer_1_out), .WE(regwe), .rd(rd), .rs(rs), .select1(rdidx), .select2(rsidx), .Clock(clock));
  Multiplexer #(.width(8)) multiplexer_2 (.in0(rs), .in1(imm), .out(multiplexer_2_out), .sel(alusrc));  // open: en
  ALU u_ALU (.Carry_in(Ci), .A(rd), .B(multiplexer_2_out), .Op(aluop), .Result(alu), .Carry_Out(ALU_carry_out));
  RAM #(.bus("separate")) ram_1 (.addr(rs), .din(rd), .data(data), .str(memwe), .clk(clock));  // open: sel, ld, clr
  Register #(.width(1)) register_1 (.D(ALU_carry_out), .Q(Ci), .clk(clock));  // open: en, clr

  // Other names for the same wires on the sheet: Co = Ci

  // Notes on the sheet:
  //   value of PC Reg
  //   address to store
  //   data to store
  //   PLEASE NOTE: I WOULD HAVE MADE IT MORE PRETTY...
  //   BUT I DONT WANT TO MESS ANY OF THE WIRES UP
  //   BUT IT WORKS 100%
  //   SO YAY!
  //   str = write enable
  //   data to load
endmodule

module Display (
  input  [7:0] hi,
  input  [7:0] lo,
  input  Enable,
  input  Clock,
  output [3:0] hi_2,
  output [3:0] lo_2,
  output [3:0] lo_3,
  output [3:0] lo_4
);

  Register register_1 (.D(hi), .en(Enable), .Q({hi_2, lo_2}), .clk(Clock));  // open: clr
  Register register_2 (.D(lo), .en(Enable), .Q({lo_3, lo_4}), .clk(Clock));  // open: clr
endmodule

module ALU (
  input  Carry_in,
  input  [7:0] A,
  input  [7:0] B,
  input  [3:0] Op,
  output [7:0] Result,
  output Carry_Out
);

  wire Carry_out___IN, Carry_out___IN_t, Carry_out_minus, Carry_out_plus, Carry_out_r, Carry_out_R_IN;
  wire [7:0] adder_1_out, adder_2_out, and_1_out, not_1_p2, or_1_out, shifter_1_out, shifter_2_out,
       subtractor_1_out, subtractor_2_out, subtractor_3_out, subtractor_4_out, undriven;

  assign and_1_out = A & B & undriven;  // AND_Gate and_1, 8 bits wide
  assign or_1_out = undriven | A | B;  // OR_Gate or_1, 8 bits wide
  // NOT_Gate #(.width(8)) not_1: pin names not known; wires that end beside it: B, not_1_p2
  Adder adder_1 (.a(A), .b(B), .out(adder_1_out), .cout(Carry_out_plus));  // open: cin
  Subtractor subtractor_1 (.a(A), .b(B), .out(subtractor_1_out), .bout(Carry_out_minus));  // open: bin
  Subtractor subtractor_2 (.a(B), .b(A), .out(subtractor_2_out), .bout(Carry_out_r));  // open: bin
  Adder adder_2 (.a(A), .b(B), .out(adder_2_out), .cin(Carry_in), .cout(Carry_out___IN));
  Subtractor subtractor_3 (.a(A), .b(B), .out(subtractor_3_out), .bin(Carry_in), .bout(Carry_out___IN_t));
  Subtractor subtractor_4 (.a(B), .b(A), .out(subtractor_4_out), .bin(Carry_in), .bout(Carry_out_R_IN));
  Shifter shifter_1 (.in(A), .\dist (B[2:0]), .out(shifter_1_out));
  Shifter #(.shift("lr")) shifter_2 (.in(A), .\dist (B[2:0]), .out(shifter_2_out));
  Multiplexer #(.select(4), .width(8)) multiplexer_1 (
    .in1(adder_1_out), .in2(subtractor_1_out), .in3(subtractor_2_out), .in4(and_1_out), .in5(or_1_out),
    .in6(not_1_p2), .in7(shifter_1_out), .in8(shifter_2_out), .in9(adder_2_out), .in10(subtractor_3_out),
    .in11(subtractor_4_out), .out(Result), .sel(Op));  // open: in0, in12, in13, in14, in15, en
  Multiplexer #(.select(4)) multiplexer_2 (
    .in1(Carry_out_plus), .in2(Carry_out_minus), .in3(Carry_out_r), .in9(Carry_out___IN),
    .in10(Carry_out___IN_t), .in11(Carry_out_R_IN), .out(Carry_Out), .sel(Op));  // open: in0, in4, in5, in6, in7, in8, in12, in13, in14, in15, en

  // Notes on the sheet:
  //   Store carry out on main! 
endmodule

module Register_File (
  input  [7:0] data,
  input  [2:0] select1,
  input  WE,
  input  [2:0] select2,
  input  Clock,
  output [7:0] rd,
  output [7:0] rs
);

  wire demultiplexer_1_out1, demultiplexer_1_out2, demultiplexer_1_out3, demultiplexer_1_out4,
       demultiplexer_1_out5, demultiplexer_1_out6, demultiplexer_1_out7;
  wire [7:0] register_1_q, register_2_q, register_3_q, register_4_q, register_5_q, register_6_q, register_7_q;

  Demultiplexer #(.select(3)) demultiplexer_1 (
    .out1(demultiplexer_1_out1), .out2(demultiplexer_1_out2), .out3(demultiplexer_1_out3),
    .out4(demultiplexer_1_out4), .out5(demultiplexer_1_out5), .out6(demultiplexer_1_out6),
    .out7(demultiplexer_1_out7), .in(WE), .sel(select1));  // open: out0, en
  Register register_1 (.D(data), .en(demultiplexer_1_out1), .Q(register_1_q), .clk(Clock));  // open: clr
  Register register_2 (.D(data), .en(demultiplexer_1_out2), .Q(register_2_q), .clk(Clock));  // open: clr
  Register register_3 (.D(data), .en(demultiplexer_1_out3), .Q(register_3_q), .clk(Clock));  // open: clr
  Register register_4 (.D(data), .en(demultiplexer_1_out4), .Q(register_4_q), .clk(Clock));  // open: clr
  Register register_5 (.D(data), .en(demultiplexer_1_out5), .Q(register_5_q), .clk(Clock));  // open: clr
  Register register_6 (.D(data), .en(demultiplexer_1_out6), .Q(register_6_q), .clk(Clock));  // open: clr
  Register register_7 (.D(data), .en(demultiplexer_1_out7), .Q(register_7_q), .clk(Clock));  // open: clr
  Multiplexer #(.select(3), .width(8)) multiplexer_1 (
    .in0({8{1'b0}}), .in1(register_1_q), .in2(register_2_q), .in3(register_3_q), .in4(register_4_q),
    .in5(register_5_q), .in6(register_6_q), .in7(register_7_q), .out(rd), .sel(select1));  // open: en
  Multiplexer #(.select(3), .width(8)) multiplexer_2 (
    .in0({8{1'b0}}), .in1(register_1_q), .in2(register_2_q), .in3(register_3_q), .in4(register_4_q),
    .in5(register_5_q), .in6(register_6_q), .in7(register_7_q), .out(rs), .sel(select2));  // open: en
endmodule

module PC (
  input  [7:0] REG_rd,
  input  [1:0] PCSrc,
  input  [7:0] imm,
  input  HALT,
  input  Clock,
  input  [2:0] btype,
  output [7:0] PC,
  output [7:0] PC_1
);

  wire and_1_out, and_2_out, and_3_out, and_4_out, bez, bgz, blz, bnz, branch, comparator_1_gt,
       comparator_2_lt, comparator_3_eq, comparator_4_eq, not_1_p2, not_2_p1;
  wire [7:0] multiplexer_1_out, multiplexer_2_out;

  Adder adder_1 (.a(PC), .b(8'h1), .out(PC_1));  // open: cin, cout
  Decoder #(.select(3)) decoder_1 (
    .out1(bgz), .out2(blz), .out3(bnz), .out4(bez), .sel(btype));  // open: out0, out5, out6, out7, en
  Multiplexer #(.select(2), .width(8)) multiplexer_1 (
    .in0(PC_1), .in1(REG_rd), .in2(imm), .in3(multiplexer_2_out), .out(multiplexer_1_out), .sel(PCSrc));  // open: en
  Multiplexer #(.width(8)) multiplexer_2 (.in0(PC_1), .in1(imm), .out(multiplexer_2_out), .sel(branch));  // open: en
  Comparator comparator_1 (.a(REG_rd), .b({8{1'b0}}), .gt(comparator_1_gt));  // open: eq, lt
  Comparator comparator_2 (.a(REG_rd), .b({8{1'b0}}), .lt(comparator_2_lt));  // open: gt, eq
  Comparator comparator_3 (.a(REG_rd), .b({8{1'b0}}), .eq(comparator_3_eq));  // open: gt, lt
  // NOT_Gate not_1: pin names not known; wires that end beside it: comparator_3_eq, not_1_p2
  Comparator comparator_4 (.a(REG_rd), .b({8{1'b0}}), .eq(comparator_4_eq));  // open: gt, lt
  Register u_PC (.D(multiplexer_1_out), .en(not_2_p1), .Q(PC), .clk(Clock));  // open: clr
  // NOT_Gate not_2: pin names not known; wires that end beside it: not_2_p1, HALT
  and and_1 (and_1_out, bgz, comparator_1_gt);
  and and_2 (and_2_out, blz, comparator_2_lt);
  and and_3 (and_3_out, bnz, not_1_p2);
  and and_4 (and_4_out, bez, comparator_4_eq);
  or or_1 (branch, and_1_out, and_2_out, and_3_out, and_4_out);

  // Other names for the same wires on the sheet: reg[7:0] = REG_rd

  // Notes on the sheet:
  //   logic here which either gives imm or PC + 1
  //   based on the branch condition
endmodule

module Control (
  input  [15:0] ROM_instruction,
  output [2:0] rdidx,
  output [2:0] rsidx,
  output [7:0] imm,
  output halt,
  output dispwe,
  output memwe,
  output [3:0] aluop,
  output alusrc,
  output regwe,
  output [1:0] regsrc,
  output [1:0] pcsrc,
  output [2:0] btype
);

  wire adc, add, adi, \and , bez, bgz, blz, bnz, j, jal, jr, ld, li, \not , \or , or_1_out, or_2_out,
       or_3_out, or_4_out, or_5_out, or_6_out, or_7_out, or_8_out, rsb, rsc, sbi, sdc, shl, shr, sli, sri,
       sub, undriven;

  or or_1 (or_1_out, j, jal);
  or or_2 (or_2_out, bnz, bez, bgz, blz);
  // Decoder #(.select(5)) decoder_1: pin names not known; wires that end beside it: ROM_instruction[15:11], halt, dispwe, li, ld, memwe, add, sub, rsb, \and , \or , \not , shl, shr, adi, sbi, sli, sri, adc, sdc, rsc, j, jr, jal, bgz, blz, bnz, bez
  Priority_Encoder #(.select(2)) priority_encoder_1 (
    .in0(or_3_out), .in1(ld), .in2(li), .in3(jal), .out(regsrc));  // open: gs, en_out, en_in
  or or_3 (or_3_out, adc, sbi, adi, add, sub, rsb, \and , \or , \not , shl, shr, sri, sli, sdc, rsc);
  Priority_Encoder #(.select(2)) priority_encoder_2 (
    .in1(jr), .in2(or_1_out), .in3(or_2_out), .out(pcsrc));  // open: in0, gs, en_out, en_in
  Priority_Encoder priority_encoder_3 (
    .in0(1'b1), .in1(bgz), .in2(blz), .in3(bnz), .in4(bez), .out(btype));  // open: in5, in6, in7, en_in, gs, en_out
  or or_4 (or_4_out, shl, sli);
  or or_5 (or_5_out, shr, sri);
  Priority_Encoder #(.select(1)) priority_encoder_4 (
    .in0(or_3_out), .in1(or_6_out), .out(alusrc));  // open: gs, en_out, en_in
  or or_6 (or_6_out, sri, sli, sbi, adi);
  or or_7 (or_7_out, add, adi, undriven);
  or or_8 (or_8_out, undriven, sub, sbi);
  Priority_Encoder #(.select(4)) priority_encoder_5 (
    .in0(1'b1), .in1(or_7_out), .in2(or_8_out), .in3(rsb), .in4(\and ), .in5(\or ), .in6(\not ),
    .in7(or_4_out), .in8(or_5_out), .in9(adc), .in10(sdc), .in11(rsc), .out(aluop));  // open: in12, in13, in14, in15, gs, en_out, en_in
  or or_9 (regwe, adc, sli, li, ld, add, sub, rsb, \and , \or , sbi, adi, \not , shl, shr, sri, rsc, sdc, jal);

  assign imm = ROM_instruction[7:0];
  assign rdidx = ROM_instruction[10:8];
  assign rsidx = ROM_instruction[2:0];

  // Other names for the same wires on the sheet: put = dispwe; opcode[4:0] = ROM_instruction[15:11]; st = memwe

  // Notes on the sheet:
  //   rs...
  //   rd...
  //   imm...
  //   opc...
endmodule
